# Fritzing sketch esp32-calendar (saved by Fritzing 1.0.4)
breadboards: 1

parts:
  S1 = Pushbutton [package="[SMD]"]
  R1 = Resistor [tolerance=±5% power=0.25W resistance=10k package=THT]
  A1 = ESP32-S3 zero
  R2 = Resistor [tolerance=±5% power=0.25W resistance=1k package=THT]
  R3 = Resistor [tolerance=±5% power=0.25W resistance=680k package=THT]
  R4 = Resistor [tolerance=±5% power=0.25W resistance=780k package=THT]
  BAT1 = Battery Holders [package=lipo-1100mAh]
  A2 = Waveshare e-Paper HAT with 7in display [package=THT]

nets:
  N1: S1.Pin_1, S1.Pin_2, A1.Pin_3, A2.pin_8
  N2: S1.Pin_3, S1.Pin_4, R1.Pin_1, R2.Pin_1
  N3: R1.Pin_0, A1.Pin_2, R4.Pin_1, BAT1.-, A2.pin_7
  N4: A1.Pin_1, R3.Pin_0, BAT1.+
  N5: A1.Pin_4, R3.Pin_1, R4.Pin_0
  N6: A1.Pin_5, R2.Pin_0
  N7: A1.Pin_7, A2.pin_1
  N8: A1.Pin_8, A2.pin_3
  N9: A1.Pin_9, A2.pin_2
  N10: A1.Pin_21, A2.pin_4
  N11: A1.Pin_25, A2.pin_6
  N12: A1.Pin_26, A2.pin_5

custom parts:
  ESP32-S3 zero: ESP32-S3 Mini Development Board, Based on ESP32-S3FH4R2 Dual-Core Processor, 240MHz Running Frequency, 2.4GHz Wi-Fi & Bluetooth 5.
  Waveshare e-Paper HAT with 7in display: .This is a universal driver board for e-Paper raw panels, can be used to drive various SPI interface e-Paper from Waveshare. This version includes a 7in display panel in breadboard.
